// Logisim project ALU.circ as structural Verilog: 1 circuit, main circuit main
module main (
  input  A3,
  input  B3,
  input  A2,
  input  B2,
  input  A1,
  input  B1,
  input  A0,
  input  B0,
  input  MSB,
  input  in_10,
  input  in_11,
  input  LSB,
  output out_13,
  output out_14,
  output out_15,
  output out_16
);

  wire A_B_2_out, A_B_3_out, A_B_4_out, A_B_out, A_nB_2_out, A_nB_3_out, A_nB_4_out, A_nB_5_out, A_nB_6_out,
       A_nB_7_out, A_nB_8_out, A_nB_out, and_1_out, and_2_out, and_3_out, And_4_out, and_5_out, and_6_out,
       And_7_out, and_8_out, and_9_out, And_10_out, and_11_out, and_12_out, And_13_out, and_14_out,
       and_15_out, and_16_out, and_17_out, and_18_out, and_19_out, and_20_out, and_21_out, and_22_out,
       and_23_out, and_24_out, and_25_out, and_26_out, and_27_out, Cout_2_out, Cout_3_out, Cout_out,
       decoder_1_out0, decoder_1_out1, decoder_1_out2, decoder_1_out4, decoder_1_out5, decoder_1_out6,
       decoder_1_out7, decoder_1_out8, decoder_1_out9, multiplexer_1_out, multiplexer_2_out,
       multiplexer_3_out, multiplexer_4_out, multiplexer_5_out, multiplexer_6_out, multiplexer_7_out,
       multiplexer_8_out, multiplexer_9_out, multiplexer_10_out, multiplexer_11_out, multiplexer_12_out,
       not_1_out, not_2_out, not_3_out, not_4_out, not_5_out, not_6_out, not_7_out, not_8_out, not_9_out,
       not_10_out, not_11_out, not_12_out, or_1_out, or_2_out, Or_3_out, or_4_out, or_5_out, or_6_out,
       or_7_out, Or_8_out, or_9_out, or_10_out, or_11_out, Or_12_out, Or_13_out, or_14_out, or_15_out,
       or_16_out, or_17_out, or_18_out, or_19_out, or_20_out, or_21_out, or_22_out, or_23_out, or_24_out,
       or_25_out, or_26_out, or_27_out, or_28_out, or_29_out, or_30_out, S_2_out, S_3_out, S_4_out, S_out,
       SLT_out, Sum_2_out, Sum_3_out, Sum_4_out, Sum_out, xor_2_out, xor_3_out, xor_4_out, xor_out;

  Multiplexer multiplexer_1 (.in0(B3), .in1(not_1_out), .out(multiplexer_1_out), .sel(or_11_out));  // open: en
  xor \xor  (xor_out, A3, multiplexer_1_out);
  xor S (S_out, Cout_out, xor_out);
  and and_1 (and_1_out, or_1_out, S_out);
  Decoder #(.select(4)) decoder_1 (
    .out0(decoder_1_out0), .out1(decoder_1_out1), .out2(decoder_1_out2), .out4(decoder_1_out4),
    .out5(decoder_1_out5), .out6(decoder_1_out6), .out7(decoder_1_out7), .out8(decoder_1_out8),
    .out9(decoder_1_out9), .sel({MSB, in_10, in_11, LSB}));  // open: out3, out10, out11, out12, out13, out14, out15, en
  or or_1 (or_1_out, B3, B0, B2, B1);
  not not_1 (not_1_out, B3);
  and and_2 (and_2_out, A2, multiplexer_2_out);
  xor Cout (Cout_out, and_2_out, and_3_out);
  and and_3 (and_3_out, xor_2_out, Cout_2_out);
  Multiplexer multiplexer_2 (.in0(B2), .in1(not_2_out), .out(multiplexer_2_out), .sel(or_11_out));  // open: en
  xor xor_2 (xor_2_out, A2, multiplexer_2_out);
  xor S_2 (S_2_out, Cout_2_out, xor_2_out);
  and Sum (Sum_out, S_out, decoder_1_out2);
  and And_4 (And_4_out, and_12_out, decoder_1_out0);
  or or_2 (or_2_out, Sum_out, And_4_out, Or_3_out);
  not not_2 (not_2_out, B2);
  and and_5 (and_5_out, A1, multiplexer_3_out);
  xor Cout_2 (Cout_2_out, and_5_out, and_6_out);
  and and_6 (and_6_out, xor_3_out, Cout_3_out);
  and Or_3 (Or_3_out, or_15_out, decoder_1_out1);
  or or_4 (or_4_out, or_6_out, or_20_out);
  or or_5 (or_5_out, or_2_out, or_16_out);
  or _8 (out_13, or_5_out, or_27_out);
  Multiplexer multiplexer_3 (.in0(B1), .in1(not_3_out), .out(multiplexer_3_out), .sel(or_11_out));  // open: en
  xor xor_3 (xor_3_out, A1, multiplexer_3_out);
  xor S_3 (S_3_out, Cout_3_out, xor_3_out);
  and Sum_2 (Sum_2_out, S_2_out, decoder_1_out2);
  and And_7 (And_7_out, and_11_out, decoder_1_out0);
  or or_6 (or_6_out, Sum_2_out, And_7_out, Or_8_out);
  or or_7 (or_7_out, or_10_out, or_24_out);
  or _2 (out_15, or_7_out, or_29_out);
  or _4 (out_14, or_4_out, or_28_out);
  not not_3 (not_3_out, B1);
  and and_8 (and_8_out, A0, multiplexer_4_out);
  xor Cout_3 (Cout_3_out, and_8_out, and_9_out);
  and and_9 (and_9_out, xor_4_out, or_11_out);
  and Or_8 (Or_8_out, or_18_out, decoder_1_out1);
  or or_9 (or_9_out, or_14_out, or_26_out);
  or _1 (out_16, or_9_out, or_30_out);
  not not_4 (not_4_out, B0);
  Multiplexer multiplexer_4 (.in0(B0), .in1(not_4_out), .out(multiplexer_4_out), .sel(or_11_out));  // open: en
  xor xor_4 (xor_4_out, A0, multiplexer_4_out);
  xor S_4 (S_4_out, or_11_out, xor_4_out);
  and And_10 (And_10_out, and_15_out, decoder_1_out0);
  and Sum_3 (Sum_3_out, S_3_out, decoder_1_out2);
  or or_10 (or_10_out, Sum_3_out, And_10_out, Or_12_out);
  or or_11 (or_11_out, decoder_1_out6, decoder_1_out7);
  and Sum_4 (Sum_4_out, S_4_out, decoder_1_out2);
  and Or_12 (Or_12_out, or_17_out, decoder_1_out1);
  and and_11 (and_11_out, B2, A2);
  and and_12 (and_12_out, B3, A3);
  and Or_13 (Or_13_out, or_19_out, decoder_1_out1);
  and And_13 (And_13_out, and_14_out, decoder_1_out0);
  or or_14 (or_14_out, Sum_4_out, And_13_out, Or_13_out);
  and and_14 (and_14_out, B0, A0);
  and and_15 (and_15_out, B1, A1);
  or or_15 (or_15_out, B3, A3);
  and A_nB (A_nB_out, and_17_out, decoder_1_out4);
  and A_nB_2 (A_nB_2_out, or_23_out, decoder_1_out5);
  and A_B (A_B_out, S_out, decoder_1_out6);
  or or_16 (or_16_out, A_nB_out, A_nB_2_out, A_B_out, SLT_out);
  or or_17 (or_17_out, B1, A1);
  or or_18 (or_18_out, B2, A2);
  and SLT (SLT_out, and_1_out, decoder_1_out7);
  or or_19 (or_19_out, B0, A0);
  not not_5 (not_5_out, B2);
  not not_6 (not_6_out, B3);
  and and_16 (and_16_out, A2, not_5_out);
  and and_17 (and_17_out, A3, not_6_out);
  and A_nB_3 (A_nB_3_out, and_16_out, decoder_1_out4);
  and A_nB_4 (A_nB_4_out, or_22_out, decoder_1_out5);
  and A_B_2 (A_B_2_out, S_2_out, decoder_1_out6);
  or or_20 (or_20_out, A_nB_3_out, A_nB_4_out, A_B_2_out);
  not not_7 (not_7_out, B0);
  not not_8 (not_8_out, B1);
  and and_18 (and_18_out, A0, not_7_out);
  and and_19 (and_19_out, A1, not_8_out);
  not not_9 (not_9_out, B2);
  or or_21 (or_21_out, A1, not_12_out);
  not not_10 (not_10_out, B3);
  or or_22 (or_22_out, A2, not_9_out);
  or or_23 (or_23_out, A3, not_10_out);
  and A_nB_5 (A_nB_5_out, or_21_out, decoder_1_out5);
  and A_B_3 (A_B_3_out, S_3_out, decoder_1_out6);
  and A_nB_6 (A_nB_6_out, and_19_out, decoder_1_out4);
  or or_24 (or_24_out, A_nB_6_out, A_nB_5_out, A_B_3_out);
  not not_11 (not_11_out, B0);
  not not_12 (not_12_out, B1);
  or or_25 (or_25_out, A0, not_11_out);
  and A_nB_7 (A_nB_7_out, and_18_out, decoder_1_out4);
  and A_B_4 (A_B_4_out, S_4_out, decoder_1_out6);
  and A_nB_8 (A_nB_8_out, or_25_out, decoder_1_out5);
  or or_26 (or_26_out, A_nB_7_out, A_nB_8_out, A_B_4_out);
  Multiplexer #(.select(2)) multiplexer_5 (
    .in0(A3), .in1(A2), .in2(A1), .in3(A0), .out(multiplexer_5_out), .sel({B1, B0}));  // open: en
  and and_20 (and_20_out, multiplexer_5_out, decoder_1_out8);
  or or_27 (or_27_out, and_20_out, and_24_out);
  Multiplexer #(.select(2)) multiplexer_6 (
    .in0(A2), .in1(A1), .in2(A0), .in3(1'b0), .out(multiplexer_6_out), .sel({B1, B0}));  // open: en
  and and_21 (and_21_out, multiplexer_6_out, decoder_1_out8);
  or or_28 (or_28_out, and_21_out, and_25_out);
  Multiplexer #(.select(2)) multiplexer_7 (
    .in0(A1), .in1(A0), .in2(1'b0), .in3(1'b0), .out(multiplexer_7_out), .sel({B1, B0}));  // open: en
  and and_22 (and_22_out, multiplexer_7_out, decoder_1_out8);
  or or_29 (or_29_out, and_22_out, and_26_out);
  Multiplexer #(.select(2)) multiplexer_8 (
    .in0(A0), .in1(1'b0), .in2(1'b0), .in3(1'b0), .out(multiplexer_8_out), .sel({B1, B0}));  // open: en
  and and_23 (and_23_out, multiplexer_8_out, decoder_1_out8);
  or or_30 (or_30_out, and_23_out, and_27_out);
  Multiplexer #(.select(2)) multiplexer_9 (
    .in0(A3), .in1(1'b0), .in2(1'b0), .in3(1'b0), .out(multiplexer_9_out), .sel({B1, B0}));  // open: en
  and and_24 (and_24_out, multiplexer_9_out, decoder_1_out9);
  Multiplexer #(.select(2)) multiplexer_10 (
    .in0(A2), .in1(A3), .in2(1'b0), .in3(1'b0), .out(multiplexer_10_out), .sel({B1, B0}));  // open: en
  and and_25 (and_25_out, multiplexer_10_out, decoder_1_out9);
  Multiplexer #(.select(2)) multiplexer_11 (
    .in0(A1), .in1(A2), .in2(A3), .in3(1'b0), .out(multiplexer_11_out), .sel({B1, B0}));  // open: en
  and and_26 (and_26_out, multiplexer_11_out, decoder_1_out9);
  Multiplexer #(.select(2)) multiplexer_12 (
    .in0(A0), .in1(A1), .in2(A2), .in3(A3), .out(multiplexer_12_out), .sel({B1, B0}));  // open: en
  and and_27 (and_27_out, multiplexer_12_out, decoder_1_out9);
endmodule
