// Logisim project ArsalanIravani_2623.circ as structural Verilog: 1 circuit, main circuit main
module main (
);

  wire and_1_out, and_2_out, and_3_out, and_4_out, and_5_out, and_6_out, and_7_out, and_8_out, clock_1_out,
       d_ff_1_q, d_ff_2_q, d_ff_3_q, d_ff_4_q, decoder_1_out0, decoder_1_out1, decoder_1_out2,
       decoder_1_out3, decoder_1_out4, decoder_1_out5, decoder_1_out6, decoder_1_out7, decoder_1_out8,
       decoder_1_out9, decoder_1_out10, decoder_1_out11, decoder_1_out12, decoder_1_out13, decoder_1_out14,
       decoder_1_out15, not_1_out, not_2_out, not_3_out, not_4_out, or_1_out, or_2_out, or_3_out, or_4_out,
       or_5_out, or_6_out, or_7_out, or_8_out, or_9_out;
  wire [3:0] d_ff_1_qn;

  not not_1 (not_1_out, 1'b1);
  not not_2 (not_2_out, 1'b1);
  and and_1 (and_1_out, d_ff_1_qn[0], 1'b1);
  and and_2 (and_2_out, not_1_out, d_ff_1_q);
  and and_3 (and_3_out, d_ff_1_qn[3], 1'b1);
  and and_4 (and_4_out, not_2_out, d_ff_2_q);
  Clock clock_1 (.out(clock_1_out));
  or or_1 (or_1_out, and_1_out, and_2_out);
  or or_2 (or_2_out, and_3_out, and_4_out);
  D_Flip_Flop d_ff_1 (.clk(clock_1_out), .D(or_1_out), .Q(d_ff_1_q), .Qn(d_ff_1_qn[0]));  // open: preset, en, reset
  D_Flip_Flop d_ff_2 (.clk(d_ff_4_q), .D(or_2_out), .Q(d_ff_2_q), .Qn(d_ff_1_qn[3]));  // open: preset, en, reset
  not not_3 (not_3_out, 1'b1);
  not not_4 (not_4_out, 1'b1);
  and and_5 (and_5_out, d_ff_1_qn[1], 1'b1);
  or or_3 (or_3_out, and_5_out, and_6_out);
  and and_6 (and_6_out, not_3_out, d_ff_3_q);
  and and_7 (and_7_out, d_ff_1_qn[2], 1'b1);
  or or_4 (or_4_out, and_7_out, and_8_out);
  and and_8 (and_8_out, not_4_out, d_ff_4_q);
  Decoder #(.select(4), .enable("false")) decoder_1 (
    .out0(decoder_1_out0), .out1(decoder_1_out1), .out2(decoder_1_out2), .out3(decoder_1_out3),
    .out4(decoder_1_out4), .out5(decoder_1_out5), .out6(decoder_1_out6), .out7(decoder_1_out7),
    .out8(decoder_1_out8), .out9(decoder_1_out9), .out10(decoder_1_out10), .out11(decoder_1_out11),
    .out12(decoder_1_out12), .out13(decoder_1_out13), .out14(decoder_1_out14), .out15(decoder_1_out15),
    .sel(d_ff_1_qn));
  D_Flip_Flop d_ff_3 (.clk(d_ff_1_q), .D(or_3_out), .Q(d_ff_3_q), .Qn(d_ff_1_qn[1]));  // open: preset, en, reset
  D_Flip_Flop d_ff_4 (.clk(d_ff_3_q), .D(or_4_out), .Q(d_ff_4_q), .Qn(d_ff_1_qn[2]));  // open: preset, en, reset
  or or_5 (or_5_out, decoder_1_out0, decoder_1_out1, decoder_1_out2);
  or or_6 (or_6_out, decoder_1_out3, decoder_1_out4, decoder_1_out5, decoder_1_out6, decoder_1_out7);
  or or_7 (or_7_out, decoder_1_out8, decoder_1_out9, decoder_1_out10);
  or or_8 (or_8_out, decoder_1_out11, decoder_1_out12, decoder_1_out13, decoder_1_out14, decoder_1_out15);
  LED led_1 (.in(or_5_out));
  LED led_2 (.in(or_9_out));
  or or_9 (or_9_out, or_6_out, or_8_out);
  LED led_3 (.in(or_7_out));

  // Notes on the sheet:
  //   First
  //   Fourth
  //   Third
  //   Second
  //   Red
  //   Orange
  //   Green
endmodule
