// Logisim project Arsalan_Iravani_float.circ as structural Verilog: 1 circuit, main circuit main
module main (
  input  in_1,
  input  in_2,
  input  in_3,
  input  in_4,
  input  in_5,
  input  in_6,
  input  in_7,
  input  in_8,
  input  in_9,
  input  in_10,
  input  in_11,
  input  in_12,
  input  in_13,
  input  in_14,
  input  in_15,
  input  in_16,
  input  in_17,
  input  in_18,
  output out_19,
  output out_20,
  output out_21,
  output out_22,
  output out_23,
  output out_24,
  output out_25,
  output out_26,
  output out_27
);

  wire comparator_1_gt, subtractor_1_bout;
  wire [0:0] adder_2_cout;
  wire [2:0] multiplexer_1_out, subtractor_1_out;
  wire [4:0] adder_2_out, multiplexer_2_out, multiplexer_3_out, shifter_1_out;

  Subtractor #(.width(3)) subtractor_1 (
    .a({in_11, in_12, in_13}), .b({in_2, in_3, in_4}), .out(subtractor_1_out), .bout(subtractor_1_bout));  // open: bin
  Comparator #(.width(3)) comparator_1 (
    .a({in_11, in_12, in_13}), .b({in_2, in_3, in_4}), .gt(comparator_1_gt));  // open: eq, lt
  Multiplexer #(.width(3)) multiplexer_1 (
    .in0({in_11, in_12, in_13}), .in1({in_2, in_3, in_4}), .out(multiplexer_1_out), .sel(comparator_1_gt));  // open: en
  and and_1 (out_19, in_1, in_10);
  Adder #(.width(3)) adder_1 (
    .a(multiplexer_1_out), .b({2'b00, adder_2_cout[0]}), .out({out_20, out_21, out_22}));  // open: cin, cout
  Multiplexer #(.width(5)) multiplexer_2 (
    .in0({in_5, in_6, in_7, in_8, in_9}), .in1({in_14, in_15, in_16, in_17, in_18}), .out(multiplexer_2_out),
    .sel(subtractor_1_bout));  // open: en
  Shifter #(.width(5), .shift("ar")) shifter_1 (.in(multiplexer_2_out), .\dist (subtractor_1_out), .out(shifter_1_out));
  Multiplexer #(.width(5)) multiplexer_3 (
    .in0({in_14, in_15, in_16, in_17, in_18}), .in1({in_5, in_6, in_7, in_8, in_9}), .out(multiplexer_3_out),
    .sel(subtractor_1_bout));  // open: en
  Adder #(.width(5)) adder_2 (
    .a(multiplexer_3_out), .b(shifter_1_out), .out(adder_2_out), .cout(adder_2_cout[0]));  // open: cin
  Shifter #(.width(5), .shift("ar")) shifter_2 (
    .in(adder_2_out), .\dist ({2'b00, adder_2_cout[0]}), .out({out_23, out_24, out_25, out_26, out_27}));
endmodule
