// Logisim project arsalan_iravani_2018_divisible.circ as structural Verilog: 1 circuit, main circuit main
module main (
  input  B3,
  input  B2,
  input  B1,
  input  B0,
  input  A3,
  input  A2,
  input  A1,
  input  A0
);

  wire and_1_out, and_2_out, and_3_out, and_4_out, and_5_out, and_6_out, and_7_out, and_8_out, and_9_out,
       and_10_out, clock_1_out, Clock_2_out, clock_3_out, clock_4_out, Cout_2_out, Cout_3_out, Cout_out,
       LSB_2_q, LSB_3_q, LSB_3_qn, LSB_4_q, LSB_5_q, LSB_6_q, LSB_7_q, LSB_q, multiplexer_2_out,
       multiplexer_3_out, multiplexer_4_out, multiplexer_5_out, nor_1_out, not_1_out, not_2_out, not_3_out,
       not_4_out, not_5_out, not_6_out, not_7_out, not_8_out, not_9_out, not_10_out, not_11_out, not_12_out,
       or_1_out, or_2_out, SLT_out, State_2_q, State_3_q, State_4_q, State_q, xor_2_out, xor_3_out,
       xor_4_out, xor_out, YES_out;
  wire [3:0] multiplexer_1_out, S_4_out;

  or or_1 (or_1_out, LSB_6_q, LSB_5_q);
  not not_1 (not_1_out, or_1_out);
  Clock clock_1 (.out(clock_1_out));
  Clock Clock_2 (.out(Clock_2_out));
  and and_1 (and_1_out, Clock_2_out, not_1_out, not_2_out);
  Multiplexer #(.width(4)) multiplexer_1 (
    .in0({A3, A2, A1, A0}), .in1(S_4_out), .out(multiplexer_1_out), .sel(LSB_q), .en(not_2_out));
  not not_2 (not_2_out, and_10_out);
  D_Flip_Flop LSB (.clk(LSB_3_q), .D(1'b1), .Q(LSB_q));  // open: Qn, preset, en, reset
  D_Flip_Flop LSB_2 (.clk(clock_1_out), .D(SLT_out), .Q(LSB_2_q));  // open: Qn, preset, en, reset
  not not_3 (not_3_out, LSB_2_q);
  D_Flip_Flop State (.clk(and_1_out), .D(multiplexer_1_out[0]), .Q(State_q));  // open: Qn, preset, en, reset
  D_Flip_Flop State_2 (.clk(and_1_out), .D(multiplexer_1_out[1]), .Q(State_2_q));  // open: Qn, preset, en, reset
  D_Flip_Flop State_3 (.clk(and_1_out), .D(multiplexer_1_out[2]), .Q(State_3_q));  // open: Qn, preset, en, reset
  D_Flip_Flop State_4 (.clk(and_1_out), .D(multiplexer_1_out[3]), .Q(State_4_q));  // open: Qn, preset, en, reset
  D_Flip_Flop LSB_3 (.clk(and_1_out), .D(LSB_3_qn), .Q(LSB_3_q), .Qn(LSB_3_qn));  // open: preset, en, reset
  and and_2 (and_2_out, SLT_out, LSB_q, not_3_out);
  not not_4 (not_4_out, LSB_6_q);
  xor S (S_4_out[3], Cout_out, xor_out);
  and SLT (SLT_out, or_2_out, S_4_out[3]);
  and and_3 (and_3_out, and_2_out, not_4_out);
  or or_2 (or_2_out, State_q, B0, B2, B1);
  not not_5 (not_5_out, B3);
  Multiplexer multiplexer_2 (.in0(B3), .in1(not_5_out), .out(multiplexer_2_out), .sel(1'b1));  // open: en
  xor Cout (Cout_out, and_4_out, and_5_out);
  xor \xor  (xor_out, State_4_q, multiplexer_2_out);
  Clock clock_3 (.out(clock_3_out));
  D_Flip_Flop LSB_4 (.clk(clock_3_out), .D(and_3_out), .Q(LSB_4_q));  // open: Qn, preset, en, reset
  and and_4 (and_4_out, State_3_q, multiplexer_3_out);
  and and_5 (and_5_out, xor_2_out, Cout_2_out);
  xor S_2 (S_4_out[2], Cout_2_out, xor_2_out);
  not not_6 (not_6_out, B2);
  Multiplexer multiplexer_3 (.in0(B2), .in1(not_6_out), .out(multiplexer_3_out), .sel(1'b1));  // open: en
  xor Cout_2 (Cout_2_out, and_6_out, and_7_out);
  xor xor_2 (xor_2_out, State_3_q, multiplexer_3_out);
  D_Flip_Flop LSB_5 (.clk(LSB_4_q), .D(1'b1), .Q(LSB_5_q));  // open: Qn, preset, en, reset
  and and_6 (and_6_out, State_2_q, multiplexer_4_out);
  and and_7 (and_7_out, xor_3_out, Cout_3_out);
  xor S_3 (S_4_out[1], Cout_3_out, xor_3_out);
  not not_7 (not_7_out, B1);
  Multiplexer multiplexer_4 (.in0(B1), .in1(not_7_out), .out(multiplexer_4_out), .sel(1'b1));  // open: en
  xor Cout_3 (Cout_3_out, and_8_out, and_9_out);
  xor xor_3 (xor_3_out, State_2_q, multiplexer_4_out);
  and and_8 (and_8_out, State_q, multiplexer_5_out);
  xor xor_4 (xor_4_out, State_q, multiplexer_5_out);
  and and_9 (and_9_out, xor_4_out, 1'b1);
  xor S_4 (S_4_out[0], 1'b1, xor_4_out);
  and and_10 (and_10_out, S_4_out[0], S_4_out[1], S_4_out[2], S_4_out[3]);
  not not_8 (not_8_out, B0);
  Multiplexer multiplexer_5 (.in0(B0), .in1(not_8_out), .out(multiplexer_5_out), .sel(1'b1));  // open: en
  not not_9 (not_9_out, S_4_out[0]);
  not not_10 (not_10_out, S_4_out[1]);
  not not_11 (not_11_out, S_4_out[2]);
  not not_12 (not_12_out, S_4_out[3]);
  LED In_Progress (.in(nor_1_out));
  nor nor_1 (nor_1_out, LSB_6_q, LSB_5_q);
  D_Flip_Flop LSB_6 (.clk(LSB_7_q), .D(1'b1), .Q(LSB_6_q));  // open: Qn, preset, en, reset
  Clock clock_4 (.out(clock_4_out));
  and YES (YES_out, not_9_out, not_10_out, or_2_out, not_11_out, not_12_out);
  D_Flip_Flop LSB_7 (.clk(clock_4_out), .D(YES_out), .Q(LSB_7_q));  // open: Qn, preset, en, reset
  LED Is_not_divisible (.in(LSB_5_q));
  LED Divisible (.in(LSB_6_q));
endmodule
