// Logisim project arsalan_iravani_2623_dialpad.circ as structural Verilog: 1 circuit, main circuit main
module main (
);

  wire _0_out, _1_out, _2_out, _3_out, _4_out, _5_out, _6_out, _7_out, _8_out, _9_out, and_1_out, and_2_out,
       and_3_out, and_4_out, and_5_out, and_6_out, and_7_out, and_8_out, C_out, d_ff_9_q, d_ff_14_qn,
       d_ff_19_qn, Disable_after_reaching_end_qn, LSB_qn, not_1_out, not_2_out, not_3_out, not_4_out,
       not_5_out, not_6_out, not_7_out, not_8_out, not_9_out, not_10_out, not_11_out, or_5_out, or_6_out,
       or_7_out, or_8_out, or_9_out;
  wire [2:0] LSB_q;
  wire [3:0] d_ff_1_q, d_ff_5_q, d_ff_10_q, d_ff_15_q, d_ff_20_q, d_ff_24_q, multiplexer_1_out,
       multiplexer_2_out, multiplexer_3_out, multiplexer_4_out, multiplexer_5_out, multiplexer_6_out,
       or_1_out;

  or or_1 (or_1_out[0], _1_out, _3_out, _9_out, _5_out, _7_out);
  Multiplexer #(.width(4)) multiplexer_1 (
    .in0(or_1_out), .out(multiplexer_1_out), .sel(1'b0), .en(and_1_out));  // open: in1
  and and_1 (and_1_out, Disable_after_reaching_end_qn, not_1_out, not_3_out, not_2_out);
  not not_1 (not_1_out, LSB_q[2]);
  or or_2 (or_1_out[3], _8_out, _9_out);
  D_Flip_Flop d_ff_1 (.clk(multiplexer_1_out[0]), .D(1'b1), .Q(d_ff_1_q[0]), .reset(C_out));  // open: Qn, preset, en
  D_Flip_Flop d_ff_2 (.clk(multiplexer_1_out[1]), .D(1'b1), .Q(d_ff_1_q[1]), .reset(C_out));  // open: Qn, preset, en
  D_Flip_Flop d_ff_3 (.clk(multiplexer_1_out[2]), .D(1'b1), .Q(d_ff_1_q[2]), .reset(C_out));  // open: Qn, preset, en
  D_Flip_Flop d_ff_4 (.clk(multiplexer_1_out[3]), .D(1'b1), .Q(d_ff_1_q[3]), .reset(C_out));  // open: Qn, preset, en
  not not_2 (not_2_out, LSB_q[0]);
  not not_3 (not_3_out, LSB_q[1]);
  or or_3 (or_1_out[1], _7_out, _6_out, _3_out, _2_out);
  or or_4 (or_1_out[2], _4_out, _5_out, _7_out, _6_out);
  Button _7 (.out(_7_out));
  Button _8 (.out(_8_out));
  Button _4 (.out(_4_out));
  Button _5 (.out(_5_out));
  Button _1 (.out(_1_out));
  Button _2 (.out(_2_out));
  Button _0 (.out(_0_out));
  Multiplexer #(.width(4)) multiplexer_2 (
    .in0(or_1_out), .out(multiplexer_2_out), .sel(1'b0), .en(and_2_out));  // open: in1
  Button _9 (.out(_9_out));
  Button _6 (.out(_6_out));
  Button _3 (.out(_3_out));
  Button C (.out(C_out));
  D_Flip_Flop d_ff_5 (.clk(multiplexer_2_out[0]), .D(1'b1), .Q(d_ff_5_q[0]), .reset(C_out));  // open: Qn, preset, en
  D_Flip_Flop d_ff_6 (.clk(multiplexer_2_out[1]), .D(1'b1), .Q(d_ff_5_q[1]), .reset(C_out));  // open: Qn, preset, en
  D_Flip_Flop d_ff_7 (.clk(multiplexer_2_out[2]), .D(1'b1), .Q(d_ff_5_q[2]), .reset(C_out));  // open: Qn, preset, en
  D_Flip_Flop d_ff_8 (.clk(multiplexer_2_out[3]), .D(1'b1), .Q(d_ff_5_q[3]), .reset(C_out));  // open: Qn, preset, en
  and and_2 (and_2_out, not_5_out, not_4_out, LSB_q[0], Disable_after_reaching_end_qn);
  not not_4 (not_4_out, LSB_q[1]);
  not not_5 (not_5_out, LSB_q[2]);
  or or_5 (or_5_out, _7_out, _8_out, _9_out);
  or or_6 (or_6_out, _4_out, _5_out, _6_out);
  or or_7 (or_7_out, _1_out, _2_out, _3_out);
  Hex_Digit_Display hex_digit_display_1 (.value(d_ff_5_q));  // open: dp
  Hex_Digit_Display hex_digit_display_2 (.value(d_ff_1_q));  // open: dp
  Multiplexer #(.width(4)) multiplexer_3 (
    .in0(or_1_out), .out(multiplexer_3_out), .sel(1'b0), .en(and_4_out));  // open: in1
  and and_3 (and_3_out, _0_out, d_ff_9_q);
  Hex_Digit_Display hex_digit_display_3 (.value(d_ff_15_q));  // open: dp
  Hex_Digit_Display hex_digit_display_4 (.value(d_ff_10_q));  // open: dp
  and and_4 (and_4_out, not_7_out, LSB_q[1], not_6_out, Disable_after_reaching_end_qn);
  not not_6 (not_6_out, LSB_q[0]);
  not not_7 (not_7_out, LSB_q[2]);
  D_Flip_Flop Disable_after_reaching_end (
    .clk(and_5_out), .D(1'b1), .Qn(Disable_after_reaching_end_qn), .reset(C_out));  // open: Q, preset, en
  and and_5 (and_5_out, LSB_q[2], LSB_q[1], LSB_q[0]);
  or or_8 (or_8_out, or_5_out, or_6_out, or_7_out, and_3_out);
  or or_9 (or_9_out, LSB_q[0], LSB_q[1], LSB_q[2]);
  D_Flip_Flop d_ff_9 (.clk(or_9_out), .D(1'b1), .Q(d_ff_9_q), .reset(C_out));  // open: Qn, preset, en
  Hex_Digit_Display hex_digit_display_5 (.value(d_ff_24_q));  // open: dp
  Hex_Digit_Display hex_digit_display_6 (.value(d_ff_20_q));  // open: dp
  D_Flip_Flop d_ff_10 (.clk(multiplexer_3_out[0]), .D(1'b1), .Q(d_ff_10_q[0]), .reset(C_out));  // open: Qn, preset, en
  D_Flip_Flop d_ff_11 (.clk(multiplexer_3_out[1]), .D(1'b1), .Q(d_ff_10_q[1]), .reset(C_out));  // open: Qn, preset, en
  D_Flip_Flop d_ff_12 (.clk(multiplexer_3_out[2]), .D(1'b1), .Q(d_ff_10_q[2]), .reset(C_out));  // open: Qn, preset, en
  D_Flip_Flop d_ff_13 (.clk(multiplexer_3_out[3]), .D(1'b1), .Q(d_ff_10_q[3]), .reset(C_out));  // open: Qn, preset, en
  D_Flip_Flop LSB (.clk(or_8_out), .D(LSB_qn), .Q(LSB_q[0]), .Qn(LSB_qn), .reset(C_out));  // open: preset, en
  Multiplexer #(.width(4)) multiplexer_4 (
    .in0(or_1_out), .out(multiplexer_4_out), .sel(1'b0), .en(and_6_out));  // open: in1
  not not_8 (not_8_out, LSB_q[2]);
  D_Flip_Flop d_ff_14 (.clk(LSB_qn), .D(d_ff_14_qn), .Q(LSB_q[1]), .Qn(d_ff_14_qn), .reset(C_out));  // open: preset, en
  D_Flip_Flop d_ff_15 (.clk(multiplexer_4_out[0]), .D(1'b1), .Q(d_ff_15_q[0]), .reset(C_out));  // open: Qn, preset, en
  D_Flip_Flop d_ff_16 (.clk(multiplexer_4_out[1]), .D(1'b1), .Q(d_ff_15_q[1]), .reset(C_out));  // open: Qn, preset, en
  D_Flip_Flop d_ff_17 (.clk(multiplexer_4_out[2]), .D(1'b1), .Q(d_ff_15_q[2]), .reset(C_out));  // open: Qn, preset, en
  D_Flip_Flop d_ff_18 (.clk(multiplexer_4_out[3]), .D(1'b1), .Q(d_ff_15_q[3]), .reset(C_out));  // open: Qn, preset, en
  and and_6 (and_6_out, not_8_out, LSB_q[1], LSB_q[0], Disable_after_reaching_end_qn);
  D_Flip_Flop d_ff_19 (
    .clk(d_ff_14_qn), .D(d_ff_19_qn), .Q(LSB_q[2]), .Qn(d_ff_19_qn), .reset(C_out));  // open: preset, en
  Multiplexer #(.width(4)) multiplexer_5 (
    .in0(or_1_out), .out(multiplexer_5_out), .sel(1'b0), .en(and_7_out));  // open: in1
  and and_7 (and_7_out, LSB_q[2], not_9_out, not_10_out, Disable_after_reaching_end_qn);
  not not_9 (not_9_out, LSB_q[1]);
  not not_10 (not_10_out, LSB_q[0]);
  D_Flip_Flop d_ff_20 (.clk(multiplexer_5_out[0]), .D(1'b1), .Q(d_ff_20_q[0]), .reset(C_out));  // open: Qn, preset, en
  D_Flip_Flop d_ff_21 (.clk(multiplexer_5_out[1]), .D(1'b1), .Q(d_ff_20_q[1]), .reset(C_out));  // open: Qn, preset, en
  D_Flip_Flop d_ff_22 (.clk(multiplexer_5_out[2]), .D(1'b1), .Q(d_ff_20_q[2]), .reset(C_out));  // open: Qn, preset, en
  Multiplexer #(.width(4)) multiplexer_6 (
    .in0(or_1_out), .out(multiplexer_6_out), .sel(1'b0), .en(and_8_out));  // open: in1
  D_Flip_Flop d_ff_23 (.clk(multiplexer_5_out[3]), .D(1'b1), .Q(d_ff_20_q[3]), .reset(C_out));  // open: Qn, preset, en
  and and_8 (and_8_out, LSB_q[2], not_11_out, LSB_q[0], Disable_after_reaching_end_qn);
  not not_11 (not_11_out, LSB_q[1]);
  D_Flip_Flop d_ff_24 (.clk(multiplexer_6_out[0]), .D(1'b1), .Q(d_ff_24_q[0]), .reset(C_out));  // open: Qn, preset, en
  D_Flip_Flop d_ff_25 (.clk(multiplexer_6_out[1]), .D(1'b1), .Q(d_ff_24_q[1]), .reset(C_out));  // open: Qn, preset, en
  D_Flip_Flop d_ff_26 (.clk(multiplexer_6_out[2]), .D(1'b1), .Q(d_ff_24_q[2]), .reset(C_out));  // open: Qn, preset, en
  D_Flip_Flop d_ff_27 (.clk(multiplexer_6_out[3]), .D(1'b1), .Q(d_ff_24_q[3]), .reset(C_out));  // open: Qn, preset, en
endmodule
