// Logisim project lab2.circ as structural Verilog: 1 circuit, main circuit main
module main (
);

  wire _0_2_out, _0_3_out, _0_4_out, _0_5_out, _0_out, _1_2_out, _1_3_out, _1_4_out, _1_out, _2_2_out,
       _2_3_out, _2_out, _3_2_out, _3_3_out, _3_out, _4_2_out, _4_3_out, _4_out, _5_2_out, _5_out, _6_out,
       _7_out, _8_out, Clock_out, d_ff_1_qn, d_ff_2_qn, d_ff_3_qn, decoder_1_out0, decoder_1_out1,
       decoder_1_out2, decoder_1_out3, decoder_1_out4, decoder_1_out5, decoder_1_out6, decoder_1_out7,
       decoder_1_out8, decoder_1_out9, decoder_1_out10, decoder_1_out11, decoder_1_out12, decoder_1_out13,
       decoder_1_out14, decoder_1_out15, decoder_1_out16, decoder_1_out17, decoder_1_out18, decoder_1_out19,
       decoder_1_out20, decoder_1_out21, decoder_1_out22, decoder_1_out23, decoder_1_out24, decoder_1_out25,
       decoder_1_out26, decoder_1_out27, decoder_1_out28, decoder_1_out29, decoder_1_out30, decoder_1_out31,
       Enable_out, In_out, LSB_qn, MSB_qn, multiplexer_1_out, not_1_out, not_2_out, not_3_out, not_4_out,
       not_5_out, Out_out, Reset_out, State_q;
  wire [4:0] LSB_q;

  Button _1 (.out(_1_out));
  Button _0 (.out(_0_out));
  Button Reset (.out(Reset_out));
  Decoder #(.select(5), .enable("false")) decoder_1 (
    .out0(decoder_1_out0), .out1(decoder_1_out1), .out2(decoder_1_out2), .out3(decoder_1_out3),
    .out4(decoder_1_out4), .out5(decoder_1_out5), .out6(decoder_1_out6), .out7(decoder_1_out7),
    .out8(decoder_1_out8), .out9(decoder_1_out9), .out10(decoder_1_out10), .out11(decoder_1_out11),
    .out12(decoder_1_out12), .out13(decoder_1_out13), .out14(decoder_1_out14), .out15(decoder_1_out15),
    .out16(decoder_1_out16), .out17(decoder_1_out17), .out18(decoder_1_out18), .out19(decoder_1_out19),
    .out20(decoder_1_out20), .out21(decoder_1_out21), .out22(decoder_1_out22), .out23(decoder_1_out23),
    .out24(decoder_1_out24), .out25(decoder_1_out25), .out26(decoder_1_out26), .out27(decoder_1_out27),
    .out28(decoder_1_out28), .out29(decoder_1_out29), .out30(decoder_1_out30), .out31(decoder_1_out31),
    .sel(LSB_q));
  not not_1 (not_1_out, _0_out);
  or Enable (Enable_out, _1_out, _0_out);
  and In (In_out, _1_out, not_1_out);
  not not_2 (not_2_out, In_out);
  Multiplexer multiplexer_1 (.in0(State_q), .in1(not_2_out), .out(multiplexer_1_out), .sel(Enable_out));  // open: en
  D_Flip_Flop LSB (.clk(Out_out), .D(LSB_qn), .Q(LSB_q[0]), .Qn(LSB_qn), .reset(Reset_out));  // open: preset, en
  Clock Clock (.out(Clock_out));
  D_Flip_Flop d_ff_1 (
    .clk(LSB_qn), .D(d_ff_1_qn), .Q(LSB_q[1]), .Qn(d_ff_1_qn), .reset(Reset_out));  // open: preset, en
  or _0_2 (_0_2_out, decoder_1_out0, decoder_1_out10, decoder_1_out20, decoder_1_out30);
  or _1_2 (_1_2_out, decoder_1_out1, decoder_1_out11, decoder_1_out21, decoder_1_out31);
  or _2 (_2_out, decoder_1_out2, decoder_1_out12, decoder_1_out22);
  or _3 (_3_out, decoder_1_out3, decoder_1_out13, decoder_1_out23);
  or _4 (_4_out, decoder_1_out4, decoder_1_out14, decoder_1_out24);
  or _5 (_5_out, decoder_1_out5, decoder_1_out15, decoder_1_out25);
  or _6 (_6_out, decoder_1_out6, decoder_1_out16, decoder_1_out26);
  or _7 (_7_out, decoder_1_out7, decoder_1_out17, decoder_1_out27);
  or _8 (_8_out, decoder_1_out8, decoder_1_out18, decoder_1_out28);
  D_Flip_Flop State (.clk(Clock_out), .D(multiplexer_1_out), .Q(State_q));  // open: Qn, preset, en, reset
  D_Flip_Flop d_ff_2 (
    .clk(d_ff_1_qn), .D(d_ff_2_qn), .Q(LSB_q[2]), .Qn(d_ff_2_qn), .reset(Reset_out));  // open: preset, en
  or _0_3 (_0_3_out, decoder_1_out9, decoder_1_out0, decoder_1_out1, decoder_1_out2, decoder_1_out3, decoder_1_out4, decoder_1_out5, decoder_1_out6, decoder_1_out7, decoder_1_out8);
  or _1_3 (_1_3_out, decoder_1_out14, decoder_1_out10, decoder_1_out11, decoder_1_out12, decoder_1_out13, decoder_1_out15, decoder_1_out16, decoder_1_out17, decoder_1_out18, decoder_1_out19);
  or _3_2 (_3_2_out, decoder_1_out30, decoder_1_out31);
  and Out (Out_out, State_q, In_out);
  or _2_2 (_2_2_out, decoder_1_out23, decoder_1_out29, decoder_1_out20, decoder_1_out21, decoder_1_out22, decoder_1_out24, decoder_1_out25, decoder_1_out26, decoder_1_out27, decoder_1_out28);
  D_Flip_Flop d_ff_3 (
    .clk(d_ff_2_qn), .D(d_ff_3_qn), .Q(LSB_q[3]), .Qn(d_ff_3_qn), .reset(Reset_out));  // open: preset, en
  nor _0_4 (_0_4_out, _0_2_out, _1_2_out, _7_out);
  nor _1_4 (_1_4_out, _1_2_out, _2_out, _3_out, _7_out);
  nor _2_3 (_2_3_out, _1_2_out, _4_out);
  _7_Segment_Display u_7_segment_display_1 (
    .g(_0_5_out), .f(_0_3_out), .a(not_3_out), .b(1'b1), .e(_4_2_out), .d(not_3_out), .c(not_4_out));  // open: dp
  or _0_5 (_0_5_out, _2_2_out, _3_2_out);
  not not_3 (not_3_out, _1_3_out);
  D_Flip_Flop MSB (.clk(d_ff_3_qn), .D(MSB_qn), .Q(LSB_q[4]), .Qn(MSB_qn), .reset(Reset_out));  // open: preset, en
  _7_Segment_Display u_7_segment_display_2 (
    .g(_0_4_out), .f(_1_4_out), .a(_2_3_out), .b(_3_3_out), .e(_4_3_out), .d(_5_2_out), .c(not_5_out));  // open: dp
  or _4_2 (_4_2_out, _0_3_out, _2_2_out);
  not not_4 (not_4_out, _2_2_out);
  nor _3_3 (_3_3_out, _5_out, _6_out);
  or _4_3 (_4_3_out, _0_2_out, _2_out, _6_out, _8_out);
  nor _5_2 (_5_2_out, _1_2_out, _4_out, _7_out);
  not not_5 (not_5_out, _2_out);
endmodule
