// Logisim project traffic lights.circ as structural Verilog: 1 circuit, main circuit main
module main (
);

  wire _3_out, _5_out, _9_out, and_1_out, and_2_out, and_3_out, and_4_out, and_5_out, and_6_out, and_7_out,
       and_8_out, clock_1_out, d_ff_5_q, d_ff_6_q, not_1_out, or_1_out, xor_1_out, xor_2_out, xor_3_out,
       xor_4_out, xor_5_out, xor_6_out;
  wire [3:0] d_ff_1_q;

  and and_1 (and_1_out, d_ff_1_q[1], d_ff_1_q[0]);
  and and_2 (and_2_out, d_ff_1_q[2], d_ff_1_q[1], d_ff_1_q[0]);
  xor xor_1 (xor_1_out, 1'b1, d_ff_1_q[0]);
  xor xor_2 (xor_2_out, d_ff_1_q[0], d_ff_1_q[1]);
  xor xor_3 (xor_3_out, and_1_out, d_ff_1_q[2]);
  xor xor_4 (xor_4_out, and_2_out, d_ff_1_q[3]);
  and and_3 (and_3_out, xor_1_out, not_1_out);
  and and_4 (and_4_out, xor_2_out, not_1_out);
  and and_5 (and_5_out, xor_3_out, not_1_out);
  and and_6 (and_6_out, xor_4_out, not_1_out);
  not not_1 (not_1_out, or_1_out);
  Clock clock_1 (.out(clock_1_out));
  D_Flip_Flop d_ff_1 (.clk(clock_1_out), .D(and_3_out), .Q(d_ff_1_q[0]), .en(1'b1));  // open: Qn, preset, reset
  D_Flip_Flop d_ff_2 (.clk(clock_1_out), .D(and_4_out), .Q(d_ff_1_q[1]), .en(1'b1));  // open: Qn, preset, reset
  D_Flip_Flop d_ff_3 (.clk(clock_1_out), .D(and_5_out), .Q(d_ff_1_q[2]), .en(1'b1));  // open: Qn, preset, reset
  D_Flip_Flop d_ff_4 (.clk(clock_1_out), .D(and_6_out), .Q(d_ff_1_q[3]), .en(1'b1));  // open: Qn, preset, reset
  and _5 (_5_out, d_ff_1_q[0], ~d_ff_1_q[1], d_ff_1_q[2], ~d_ff_1_q[3], and_7_out);  // AND_Gate
  and _3 (_3_out, d_ff_1_q[0], d_ff_1_q[1], ~d_ff_1_q[2], ~d_ff_1_q[3], d_ff_5_q);  // AND_Gate
  and _9 (_9_out, d_ff_1_q[0], ~d_ff_1_q[1], ~d_ff_1_q[2], d_ff_1_q[3], and_8_out);  // AND_Gate
  or or_1 (or_1_out, _9_out, _3_out, _5_out);
  xor xor_5 (xor_5_out, or_1_out, d_ff_5_q);
  xor xor_6 (xor_6_out, d_ff_5_q, d_ff_6_q);
  D_Flip_Flop d_ff_5 (.clk(clock_1_out), .D(xor_5_out), .Q(d_ff_5_q), .en(or_1_out));  // open: Qn, preset, reset
  D_Flip_Flop d_ff_6 (.clk(clock_1_out), .D(xor_6_out), .Q(d_ff_6_q), .en(or_1_out));  // open: Qn, preset, reset
  and and_7 (and_7_out, ~d_ff_5_q, ~d_ff_6_q);  // AND_Gate
  and and_8 (and_8_out, ~d_ff_5_q, d_ff_6_q);  // AND_Gate
  Hex_Digit_Display hex_digit_display_1 (.value(d_ff_1_q));  // open: dp
  LED led_1 (.in(and_7_out));
  LED led_2 (.in(d_ff_5_q));
  LED led_3 (.in(and_8_out));

  // Notes on the sheet:
  //   Main Counter, counts from 0 to 9
  //   Reset main counter when it reaches necessary value
  //   if (color = red AND value = 5) OR (color = yellow AND value = 3) OR (color = green AND value = 9)
  //   Second counter from 0 to 3 (0 - RED, 1 - YELLOW, 2 - GREEN, 3 - YELLOW)
  //   EXAMPLE Traffic Lights, for delay values RED = 5, YELLOW = 3, GREEN = 9
  //   RED
  //   YELLOW
  //   GREEN
endmodule
