// Logisim project trafficLight2.circ as structural Verilog: 1 circuit, main circuit main
module main (
);

  wire and_1_out, and_2_out, and_3_out, and_4_out, and_5_out, and_6_out, and_7_out, and_8_out, and_9_out,
       and_10_out, and_11_out, and_12_out, and_13_out, and_14_out, and_15_out, and_16_out, and_17_out,
       and_18_out, and_19_out, and_20_out, and_21_out, and_22_out, and_23_out, and_24_out, clock_1_out,
       d_ff_1_q, d_ff_1_qn, d_ff_2_q, d_ff_2_qn, d_ff_3_q, d_ff_3_qn, d_ff_4_q, d_ff_4_qn, d_ff_5_q,
       d_ff_5_qn, not_1_out, not_2_out, not_3_out, not_4_out, or_1_out, or_2_out, or_3_out, or_4_out,
       or_5_out;

  Clock clock_1 (.out(clock_1_out));
  D_Flip_Flop d_ff_1 (.clk(clock_1_out), .D(d_ff_1_qn), .Q(d_ff_1_q), .Qn(d_ff_1_qn));  // open: preset, en, reset
  D_Flip_Flop d_ff_2 (.clk(d_ff_1_qn), .D(d_ff_2_qn), .Q(d_ff_2_q), .Qn(d_ff_2_qn));  // open: preset, en, reset
  not not_1 (not_1_out, d_ff_3_q);
  not not_2 (not_2_out, d_ff_4_q);
  not not_3 (not_3_out, d_ff_1_q);
  not not_4 (not_4_out, d_ff_2_q);
  D_Flip_Flop d_ff_3 (.clk(d_ff_2_qn), .D(d_ff_3_qn), .Q(d_ff_3_q), .Qn(d_ff_3_qn));  // open: preset, en, reset
  and and_1 (and_1_out, not_1_out, not_2_out);
  and and_2 (and_2_out, d_ff_3_q, not_2_out);
  and and_3 (and_3_out, d_ff_4_q, not_1_out);
  and and_4 (and_4_out, d_ff_4_q, d_ff_3_q);
  and and_5 (and_5_out, not_3_out, not_4_out);
  and and_6 (and_6_out, d_ff_1_q, not_4_out);
  and and_7 (and_7_out, d_ff_2_q, not_3_out);
  and and_8 (and_8_out, d_ff_2_q, d_ff_1_q);
  D_Flip_Flop d_ff_4 (.clk(d_ff_3_qn), .D(d_ff_4_qn), .Q(d_ff_4_q), .Qn(d_ff_4_qn));  // open: preset, en, reset
  D_Flip_Flop d_ff_5 (.clk(d_ff_4_qn), .D(d_ff_5_qn), .Q(d_ff_5_q), .Qn(d_ff_5_qn));  // open: preset, en, reset
  and and_9 (and_9_out, and_1_out, and_5_out);
  and and_10 (and_10_out, and_1_out, and_6_out);
  and and_11 (and_11_out, and_1_out, and_7_out);
  and and_12 (and_12_out, and_1_out, and_8_out);
  and and_13 (and_13_out, and_2_out, and_5_out);
  and and_14 (and_14_out, and_2_out, and_6_out);
  and and_15 (and_15_out, and_2_out, and_7_out);
  and and_16 (and_16_out, and_2_out, and_8_out);
  and and_17 (and_17_out, and_3_out, and_5_out);
  and and_18 (and_18_out, and_3_out, and_6_out);
  and and_19 (and_19_out, and_3_out, and_7_out);
  and and_20 (and_20_out, and_3_out, and_8_out);
  and and_21 (and_21_out, and_4_out, and_5_out);
  and and_22 (and_22_out, and_4_out, and_6_out);
  and and_23 (and_23_out, and_4_out, and_7_out);
  and and_24 (and_24_out, and_4_out, and_8_out);
  or or_1 (or_1_out, and_24_out, and_23_out, and_22_out, and_21_out, and_20_out);
  or or_2 (or_2_out, and_9_out, and_10_out);
  or or_3 (or_3_out, and_11_out, and_12_out, and_13_out, and_14_out, and_15_out);
  or or_4 (or_4_out, and_18_out, and_19_out, and_16_out, and_17_out);
  LED led_1 (.in(or_2_out));
  or or_5 (or_5_out, or_3_out, or_1_out);
  LED led_2 (.in(or_5_out));
  LED led_3 (.in(or_4_out));

  // Notes on the sheet:
  //   Red
  //   Yellow
  //   Green
endmodule
